// Logisim project sleepyu.circ as structural Verilog: 7 circuits, main circuit main
module main (
);

  wire instruction_decoding_1_aluop, instruction_decoding_1_memread, instruction_decoding_1_memtoreg,
       instruction_decoding_1_memwrite, instruction_decoding_1_regwrite, PC_Clock_out;
  wire [1:0] instruction_decoding_1_rd, instruction_decoding_1_rs, instruction_decoding_1_rt;
  wire [7:0] adder_1_out, execution_1_new_pc_ex, instruction_decoding_1_new_pc_id,
       instruction_fetching_1_new_pc, instruction_fetching_1_opcode, PC_q, register_file_1_regdata1,
       register_file_1_regdata2;

  Adder adder_1 (.a(8'h1), .b(PC_q), .out(adder_1_out));  // open: cin, cout
  Clock PC_Clock (.out(PC_Clock_out));
  Register PC (.D(adder_1_out), .en(1'b1), .clk(PC_Clock_out), .Q(PC_q));  // open: clr
  Instruction_Fetching instruction_fetching_1 (
    .PC(PC_q), .PC_Clock(PC_Clock_out), .New_PC(instruction_fetching_1_new_pc),
    .Opcode(instruction_fetching_1_opcode));
  Instruction_Decoding instruction_decoding_1 (
    .New_PC_IF(instruction_fetching_1_new_pc), .Opcode(instruction_fetching_1_opcode),
    .New_PC_ID(instruction_decoding_1_new_pc_id), .Rs(instruction_decoding_1_rs),
    .Rt(instruction_decoding_1_rt), .Rd(instruction_decoding_1_rd),
    .RegWrite(instruction_decoding_1_regwrite), .ALUOp(instruction_decoding_1_aluop),
    .MemRead(instruction_decoding_1_memread), .MemWrite(instruction_decoding_1_memwrite),
    .MemToReg(instruction_decoding_1_memtoreg));
  Execution execution_1 (
    .New_PC_ID(instruction_decoding_1_new_pc_id), .RegData1(register_file_1_regdata1),
    .RegData2(register_file_1_regdata2), .Rd(instruction_decoding_1_rd),
    .ALUOp(instruction_decoding_1_aluop), .MemRead(instruction_decoding_1_memread),
    .MemWrite(instruction_decoding_1_memwrite), .MemToReg(instruction_decoding_1_memtoreg),
    .New_PC_EX(execution_1_new_pc_ex));  // open: ALUResult, StoreData
  Memory_Access memory_access_1 (.New_PC_EX(execution_1_new_pc_ex));  // open: New_PC_ME
  Register_File register_file_1 (
    .ReadReg1(instruction_decoding_1_rs), .ReadReg2(instruction_decoding_1_rt),
    .WriteReg(instruction_decoding_1_rd), .RegWrite(instruction_decoding_1_regwrite),
    .RegData1(register_file_1_regdata1), .RegData2(register_file_1_regdata2));
  Write_Back write_back_1 ();

  // Notes on the sheet:
  //   Names: Yash Parmar & Nikunj Patel
  //   Pledge: I pledge my honor that I have abided by the Stevens Honor System.
endmodule

module Instruction_Fetching (
  input  [7:0] PC,
  input  PC_Clock,
  output [7:0] New_PC,
  output [7:0] Opcode
);

  RAM ram_1 (.addr(PC), .we(1'b0), .oe(1'b1), .clk(PC_Clock), .dout(Opcode));  // open: din
  Adder adder_1 (.a(8'h1), .b(PC), .out(New_PC));  // open: cin, cout

  // Notes on the sheet:
  //   Instruction Fetching Stage
endmodule

module Instruction_Decoding (
  input  [7:0] New_PC_IF,
  input  [7:0] Opcode,
  output [7:0] New_PC_ID,
  output [1:0] Rs,
  output [1:0] Rt,
  output [1:0] Rd,
  output RegWrite,
  output ALUOp,
  output MemRead,
  output MemWrite,
  output MemToReg
);

  wire decoder_1_out0;

  Decoder #(.enable("false"), .select(2)) decoder_1 (
    .out0(decoder_1_out0), .out1(ALUOp), .out2(MemRead), .out3(MemWrite), .sel(Opcode[7:6]));
  or or_1 (RegWrite, decoder_1_out0, ALUOp, MemRead);

  assign MemToReg = MemRead;
  assign New_PC_ID = New_PC_IF;
  assign Rd = Opcode[5:4];
  assign Rs = Opcode[3:2];
  assign Rt = Opcode[1:0];

  // Notes on the sheet:
  //   Rm/Rs
  //   Rn/Rt
  //   Rd
  //   Opcode
  //   Instruction Decoding Stage
  //   Boost
  //   Fall
  //   Fetch
  //   Tuck
  //   Source Register (2-bit)
  //   Target Register (2-bit)
  //   Destination Register (2-bit)
  //   MemRead (1-bit)
  //   MemToReg (1-bit)
  //   RegWrite (1-bit)
  //   ALUOp (1-bit)
  //   MemWrite (1-bit)
endmodule

module Execution (
  input  [7:0] New_PC_ID,
  input  [7:0] RegData1,
  input  [7:0] RegData2,
  input  [1:0] Rd,
  input  ALUOp,
  input  MemRead,
  input  MemWrite,
  input  MemToReg,
  output [7:0] New_PC_EX,
  output [7:0] ALUResult,
  output [7:0] StoreData
);


  assign New_PC_EX = New_PC_ID;

  // Notes on the sheet:
  //   Execution Stage
endmodule

module Memory_Access (
  input  [7:0] New_PC_EX,
  output [7:0] New_PC_ME
);


  assign New_PC_ME = New_PC_EX;

  // Notes on the sheet:
  //   Memory Access Stage
endmodule

module Write_Back (
);


  // Notes on the sheet:
  //   Write Back Stage
endmodule

module Register_File (
  input  [1:0] ReadReg1,
  input  [1:0] ReadReg2,
  input  [1:0] WriteReg,
  input  RegWrite,
  output [7:0] RegData1,
  output [7:0] RegData2
);


  // Notes on the sheet:
  //   Register File
endmodule
